// Logisim project alu.circ as structural Verilog: 16 circuits, main circuit one_bit_alu
module ByteALU (
  input  InvB,
  input  CIn,
  input  InvOut,
  input  [1:0] Op,
  input  A0,
  input  B0,
  input  A1,
  input  B1,
  input  A2,
  input  B2,
  input  A3,
  input  B3,
  input  A4,
  input  B4,
  input  A5,
  input  B5,
  input  A6,
  input  B6,
  input  A7,
  input  B7,
  output R0,
  output R1,
  output R2,
  output R3,
  output R4,
  output R5,
  output R6,
  output R7,
  output COut
);

  wire onebitalu_1_c_out, onebitalu_2_c_out, onebitalu_3_c_out, onebitalu_4_c_out, onebitalu_5_c_out,
       onebitalu_6_c_out, onebitalu_7_c_out;

  OneBitALU onebitalu_1 (
    .C_In(CIn), .A(A0), .B(B0), .InvB(InvB), .InvOut(InvOut), .Op(Op), .Result(R0), .C_Out(onebitalu_1_c_out));
  OneBitALU onebitalu_2 (
    .C_In(onebitalu_1_c_out), .A(A1), .B(B1), .InvB(InvB), .InvOut(InvOut), .Op(Op), .Result(R1),
    .C_Out(onebitalu_2_c_out));
  OneBitALU onebitalu_3 (
    .C_In(onebitalu_2_c_out), .A(A2), .B(B2), .InvB(InvB), .InvOut(InvOut), .Op(Op), .Result(R2),
    .C_Out(onebitalu_3_c_out));
  OneBitALU onebitalu_4 (
    .C_In(onebitalu_3_c_out), .A(A3), .B(B3), .InvB(InvB), .InvOut(InvOut), .Op(Op), .Result(R3),
    .C_Out(onebitalu_4_c_out));
  OneBitALU onebitalu_5 (
    .C_In(onebitalu_4_c_out), .A(A4), .B(B4), .InvB(InvB), .InvOut(InvOut), .Op(Op), .Result(R4),
    .C_Out(onebitalu_5_c_out));
  OneBitALU onebitalu_6 (
    .C_In(onebitalu_5_c_out), .A(A5), .B(B5), .InvB(InvB), .InvOut(InvOut), .Op(Op), .Result(R5),
    .C_Out(onebitalu_6_c_out));
  OneBitALU onebitalu_7 (
    .C_In(onebitalu_6_c_out), .A(A6), .B(B6), .InvB(InvB), .InvOut(InvOut), .Op(Op), .Result(R6),
    .C_Out(onebitalu_7_c_out));
  OneBitALU onebitalu_8 (
    .C_In(onebitalu_7_c_out), .A(A7), .B(B7), .InvB(InvB), .InvOut(InvOut), .Op(Op), .Result(R7), .C_Out(COut));
endmodule

module one_bit_alu (
  input  C_In,
  input  NotOutput,
  input  A,
  input  NotB,
  input  B,
  input  OP0,
  input  OP1,
  output Result,
  output Carry
);

  wire A_NOT, B_In_NOT, B_NOT, B_t, MUX_OUT, MUX_OUT_NOT, NAND_OUT, NOR_OUT, NotB_NOT, NotOutput_NOT,
       OP0_NOT, OP1_NOT, SUM_NOT, transistor_3_out, transistor_4_out, transistor_5_out, transistor_7_out,
       transistor_9_out, transistor_12_out, transistor_16_out, transistor_17_out, transistor_22_out,
       transistor_31_out, transistor_34_out, transistor_35_out, transistor_36_out, transistor_39_out,
       transistor_40_out, transistor_47_out, transistor_50_out, transistor_55_out, transistor_58_out,
       transistor_59_out, transistor_62_out, transistor_63_out, transistor_66_out, transistor_69_out,
       transistor_72_out, transmission_1_p4, transmission_3_p4, XNOR_OUT;

  Transistor transistor_1 (.in(1'b1), .out(NAND_OUT), .gate(A));
  Transistor #(.\type ("n")) transistor_2 (.in(transistor_3_out), .out(NAND_OUT), .gate(A));
  Transistor #(.\type ("n")) transistor_3 (.in(1'b0), .out(transistor_3_out), .gate(B_t));
  Transistor transistor_4 (.in(1'b1), .out(transistor_4_out), .gate(A));
  Transistor transistor_5 (.in(transistor_4_out), .out(transistor_5_out), .gate(B_t));
  Transistor #(.\type ("n")) transistor_6 (.in(transistor_7_out), .out(transistor_5_out), .gate(A));
  Transistor #(.\type ("n")) transistor_7 (.in(1'b0), .out(transistor_7_out), .gate(B_t));
  Transistor transistor_8 (.in(1'b1), .out(NAND_OUT), .gate(B_t));
  // Probe on NAND_OUT
  Transistor transistor_9 (.in(1'b1), .out(transistor_9_out), .gate(A));
  Transistor transistor_10 (.in(transistor_9_out), .out(transistor_5_out), .gate(C_In));
  Transistor #(.\type ("n")) transistor_11 (.in(transistor_12_out), .out(transistor_5_out), .gate(C_In));
  Transistor #(.\type ("n")) transistor_12 (.in(1'b0), .out(transistor_12_out), .gate(A));
  Transistor transistor_13 (.in(1'b1), .out(transistor_9_out), .gate(B_t));
  Transistor #(.\type ("n")) transistor_14 (.in(1'b0), .out(transistor_12_out), .gate(B_t));
  Transistor #(.\type ("n")) transistor_15 (.in(1'b0), .out(NOR_OUT), .gate(A));
  Transistor transistor_16 (.in(1'b1), .out(transistor_16_out), .gate(A));
  Transistor #(.\type ("n")) transistor_17 (.in(1'b0), .out(transistor_17_out), .gate(A));
  Transistor transistor_18 (.in(1'b1), .out(NotOutput_NOT), .gate(NotOutput));
  Transistor #(.\type ("n")) transistor_19 (.in(1'b0), .out(NotOutput_NOT), .gate(NotOutput));
  Transistor transistor_20 (.in(1'b1), .out(A_NOT), .gate(A));
  Transistor #(.\type ("n")) transistor_21 (.in(1'b0), .out(A_NOT), .gate(A));
  Transistor transistor_22 (.in(1'b1), .out(transistor_22_out), .gate(B_t));
  Transistor transistor_23 (.in(transistor_22_out), .out(NOR_OUT), .gate(A));
  // Probe on NOR_OUT
  Transistor transistor_24 (.in(1'b1), .out(transistor_16_out), .gate(B_t));
  Transistor #(.\type ("n")) transistor_25 (.in(1'b0), .out(transistor_17_out), .gate(B_t));
  Transistor #(.\type ("n")) transistor_26 (.in(1'b0), .out(NOR_OUT), .gate(B_t));
  Transistor transistor_27 (.in(1'b1), .out(transistor_16_out), .gate(C_In));
  Transistor #(.\type ("n")) transistor_28 (.in(1'b0), .out(transistor_17_out), .gate(C_In));
  Transistor transistor_29 (.in(transistor_16_out), .out(SUM_NOT), .gate(transistor_5_out));
  Transistor #(.\type ("n")) transistor_30 (.in(transistor_17_out), .out(SUM_NOT), .gate(transistor_5_out));
  Transistor transistor_31 (.in(1'b1), .out(transistor_31_out), .gate(A));
  Transistor transistor_32 (.in(transistor_31_out), .out(XNOR_OUT), .gate(B_t));
  Transistor #(.\type ("n")) transistor_33 (.in(transistor_34_out), .out(XNOR_OUT), .gate(A));
  Transistor #(.\type ("n")) transistor_34 (.in(1'b0), .out(transistor_34_out), .gate(B_NOT));
  Transistor transistor_35 (.in(1'b1), .out(transistor_35_out), .gate(A));
  Transistor transistor_36 (.in(transistor_35_out), .out(transistor_36_out), .gate(B_t));
  Transistor transistor_37 (.in(transistor_36_out), .out(SUM_NOT), .gate(C_In));
  Transistor #(.\type ("n")) transistor_38 (.in(transistor_39_out), .out(SUM_NOT), .gate(C_In));
  Transistor #(.\type ("n")) transistor_39 (.in(transistor_40_out), .out(transistor_39_out), .gate(B_t));
  Transistor #(.\type ("n")) transistor_40 (.in(1'b0), .out(transistor_40_out), .gate(A));
  Transistor transistor_41 (.in(1'b1), .out(B_In_NOT), .gate(B));
  Transistor #(.\type ("n")) transistor_42 (.in(1'b0), .out(B_In_NOT), .gate(B));
  Transistor transistor_43 (.in(1'b1), .out(B_NOT), .gate(B_t));
  Transistor #(.\type ("n")) transistor_44 (.in(1'b0), .out(B_NOT), .gate(B_t));
  // Probe on SUM_NOT
  Transistor transistor_45 (.in(1'b1), .out(Carry), .gate(transistor_5_out));
  Transistor #(.\type ("n")) transistor_46 (.in(1'b0), .out(Carry), .gate(transistor_5_out));
  Transistor transistor_47 (.in(1'b1), .out(transistor_47_out), .gate(A_NOT));
  Transistor transistor_48 (.in(transistor_47_out), .out(XNOR_OUT), .gate(B_NOT));
  Transistor #(.\type ("n")) transistor_49 (.in(transistor_50_out), .out(XNOR_OUT), .gate(A_NOT));
  Transistor #(.\type ("n")) transistor_50 (.in(1'b0), .out(transistor_50_out), .gate(B_t));
  // Probe on XNOR_OUT
  Transistor transistor_51 (.in(1'b1), .out(NotB_NOT), .gate(NotB));
  Transistor #(.\type ("n")) transistor_52 (.in(1'b0), .out(NotB_NOT), .gate(NotB));
  Transistor transistor_53 (.in(1'b1), .out(OP0_NOT), .gate(OP0));
  Transistor #(.\type ("n")) transistor_54 (.in(1'b0), .out(OP0_NOT), .gate(OP0));
  Transistor transistor_55 (.in(1'b1), .out(transistor_55_out), .gate(MUX_OUT));
  Transistor transistor_56 (.in(transistor_55_out), .out(Result), .gate(NotOutput));
  Transistor #(.\type ("n")) transistor_57 (.in(transistor_58_out), .out(Result), .gate(MUX_OUT));
  Transistor #(.\type ("n")) transistor_58 (.in(1'b0), .out(transistor_58_out), .gate(NotOutput_NOT));
  // Transmission_Gate transmission_1: pin names not known; wires that end beside it: NAND_OUT, OP0, OP0_NOT, transmission_1_p4
  // Transmission_Gate transmission_2: pin names not known; wires that end beside it: NOR_OUT, OP0_NOT, OP0, transmission_1_p4
  // Transmission_Gate transmission_3: pin names not known; wires that end beside it: XNOR_OUT, OP0, OP0_NOT, transmission_3_p4
  // Transmission_Gate transmission_4: pin names not known; wires that end beside it: SUM_NOT, OP0_NOT, OP0, transmission_3_p4
  Transistor transistor_59 (.in(1'b1), .out(transistor_59_out), .gate(MUX_OUT_NOT));
  Transistor transistor_60 (.in(transistor_59_out), .out(Result), .gate(NotOutput_NOT));
  Transistor #(.\type ("n")) transistor_61 (.in(transistor_62_out), .out(Result), .gate(MUX_OUT_NOT));
  Transistor #(.\type ("n")) transistor_62 (.in(1'b0), .out(transistor_62_out), .gate(NotOutput));
  Transistor transistor_63 (.in(1'b1), .out(transistor_63_out), .gate(NotB));
  Transistor transistor_64 (.in(transistor_63_out), .out(B_t), .gate(B_In_NOT));
  Transistor #(.\type ("n")) transistor_65 (.in(transistor_66_out), .out(B_t), .gate(NotB));
  Transistor #(.\type ("n")) transistor_66 (.in(1'b0), .out(transistor_66_out), .gate(B));
  Transistor transistor_67 (.in(1'b1), .out(OP1_NOT), .gate(OP1));
  Transistor #(.\type ("n")) transistor_68 (.in(1'b0), .out(OP1_NOT), .gate(OP1));
  // Transmission_Gate transmission_5: pin names not known; wires that end beside it: transmission_1_p4, OP1, OP1_NOT, MUX_OUT
  // Transmission_Gate transmission_6: pin names not known; wires that end beside it: transmission_3_p4, OP1_NOT, OP1, MUX_OUT
  Transistor transistor_69 (.in(1'b1), .out(transistor_69_out), .gate(NotB_NOT));
  Transistor transistor_70 (.in(transistor_69_out), .out(B_t), .gate(B));
  Transistor #(.\type ("n")) transistor_71 (.in(transistor_72_out), .out(B_t), .gate(NotB_NOT));
  Transistor #(.\type ("n")) transistor_72 (.in(1'b0), .out(transistor_72_out), .gate(B_In_NOT));
  Transistor transistor_73 (.in(1'b1), .out(MUX_OUT_NOT), .gate(MUX_OUT));
  Transistor #(.\type ("n")) transistor_74 (.in(1'b0), .out(MUX_OUT_NOT), .gate(MUX_OUT));

  // Other names for the same wires on the sheet: B_In = B

  // Notes on the sheet:
  //   Full adder
  //   A XNOR B
  //   MUX_OUT XNOR NotOutput
  //   B_In XOR NotB
endmodule

module test (
  input  C_In,
  input  NotOutput,
  input  A,
  input  NotB,
  input  B,
  input  OP0,
  input  OP1,
  output out_8,
  output out_9,
  output out_10,
  output out_11,
  output out_12,
  output out_13
);

  main_gates main_gates_1 (
    .C_In(C_In), .A(NotOutput), .B(A), .InvB(NotB), .InvOut(B), .Op({OP1, OP0}), .Result(out_8), .C_Out(out_9));
  OneBitALU onebitalu_1 (
    .C_In(C_In), .A(NotOutput), .B(A), .InvB(NotB), .InvOut(B), .Op({OP1, OP0}), .Result(out_10),
    .C_Out(out_11));
  one_bit_alu one_bit_alu_1 (
    .C_In(C_In), .NotOutput(NotOutput), .A(A), .NotB(NotB), .B(B), .OP0(OP0), .OP1(OP1), .Result(out_12),
    .Carry(out_13));
endmodule

module main_gates (
  input  C_In,
  input  A,
  input  B,
  input  InvB,
  input  InvOut,
  input  [1:0] Op,
  output Result,
  output C_Out
);

  wire AND_Out, B_t, multiplexer_1_out, OR_Out, Sum_Out, XOR_Out;

  xor xor_1 (B_t, B, InvB);
  and and_1 (AND_Out, A, B_t);
  or or_1 (OR_Out, A, B_t);
  xor xor_2 (XOR_Out, A, B_t);
  FullAdder fulladder_1 (.C_In(C_In), .A(A), .B(B_t), .Sum(Sum_Out), .C_Out(C_Out));
  Multiplexer #(.select(2)) multiplexer_1 (
    .in0(AND_Out), .in1(OR_Out), .in2(XOR_Out), .in3(Sum_Out), .out(multiplexer_1_out), .sel(Op));
  xor xor_3 (Result, InvOut, multiplexer_1_out);

  // Notes on the sheet:
  //   00 AND
  //   01 OR
  //   10 XOR
  //   11 ADD
endmodule

module OneBitALU (
  input  C_In,
  input  A,
  input  B,
  input  InvB,
  input  InvOut,
  input  [1:0] Op,
  output Result,
  output C_Out
);

  wire B_t, fulladder_1_sum, multiplexer_2_out, NAND_Out, NOR_Out, not_1_out, not_3_out, NSum_Out, XNOR_Out;

  not not_1 (not_1_out, B);
  Multiplexer multiplexer_1 (.in0(B), .in1(not_1_out), .out(B_t), .sel(InvB));
  nand nand_1 (NAND_Out, A, B_t);
  nor nor_1 (NOR_Out, A, B_t);
  xnor xnor_1 (XNOR_Out, A, B_t);
  FullAdder fulladder_1 (.C_In(C_In), .A(A), .B(B_t), .Sum(fulladder_1_sum), .C_Out(C_Out));
  not not_2 (NSum_Out, fulladder_1_sum);
  Multiplexer #(.select(2)) multiplexer_2 (
    .in0(NAND_Out), .in1(NOR_Out), .in2(XNOR_Out), .in3(NSum_Out), .out(multiplexer_2_out), .sel(Op));
  not not_3 (not_3_out, multiplexer_2_out);
  Multiplexer multiplexer_3 (.in0(not_3_out), .in1(multiplexer_2_out), .out(Result), .sel(InvOut));

  // Notes on the sheet:
  //   00 AND
  //   01 OR
  //   10 XOR
  //   11 ADD
endmodule

module main_gates_inverted2 (
  input  C_In,
  input  NotOutput,
  input  A,
  input  NotB,
  input  B,
  input  [1:0] Op,
  output R,
  output C_Out
);

  wire fulladder_1_sum, multiplexer_1_out, multiplexer_2_out, nand_1_out, nor_1_out, not_1_out, not_2_out,
       not_3_out, xnor_1_out;

  not not_1 (not_1_out, B);
  Multiplexer multiplexer_1 (.in0(B), .in1(not_1_out), .out(multiplexer_1_out), .sel(NotB));
  nand nand_1 (nand_1_out, A, multiplexer_1_out);
  nor nor_1 (nor_1_out, A, multiplexer_1_out);
  xnor xnor_1 (xnor_1_out, A, multiplexer_1_out);
  FullAdder fulladder_1 (.C_In(C_In), .A(A), .B(multiplexer_1_out), .Sum(fulladder_1_sum), .C_Out(C_Out));
  not not_2 (not_2_out, fulladder_1_sum);
  Multiplexer #(.select(2)) multiplexer_2 (
    .in0(nand_1_out), .in1(nor_1_out), .in2(xnor_1_out), .in3(not_2_out), .out(multiplexer_2_out), .sel(Op));
  not not_3 (not_3_out, multiplexer_2_out);
  Multiplexer multiplexer_3 (.in0(not_3_out), .in1(multiplexer_2_out), .out(R), .sel(NotOutput));

  // Notes on the sheet:
  //   00 AND
  //   01 OR
  //   10 XOR
  //   11 ADD
endmodule

module not_gate (
  input  X,
  output R
);

  Transistor transistor_1 (.in(1'b1), .out(R), .gate(X));
  Transistor #(.\type ("n")) transistor_2 (.in(1'b0), .out(R), .gate(X));
endmodule

module nand_gate (
  input  X,
  input  Y,
  output R
);

  wire transistor_3_out;

  Transistor transistor_1 (.in(1'b1), .out(R), .gate(X));
  Transistor #(.\type ("n")) transistor_2 (.in(transistor_3_out), .out(R), .gate(Y));
  Transistor #(.\type ("n")) transistor_3 (.in(1'b0), .out(transistor_3_out), .gate(X));
  Transistor transistor_4 (.in(1'b1), .out(R), .gate(Y));
endmodule

module nor_gate (
  input  X,
  input  Y,
  output R
);

  wire transistor_2_out;

  Transistor #(.\type ("n")) transistor_1 (.in(1'b0), .out(R), .gate(X));
  Transistor transistor_2 (.in(1'b1), .out(transistor_2_out), .gate(X));
  Transistor transistor_3 (.in(transistor_2_out), .out(R), .gate(Y));
  Transistor #(.\type ("n")) transistor_4 (.in(1'b0), .out(R), .gate(Y));
endmodule

module xor_gate (
  input  A,
  input  B,
  output R
);

  wire A_NOT, B_NOT, transistor_1_out, transistor_4_out, transistor_8_out;

  Transistor transistor_1 (.in(1'b1), .out(transistor_1_out), .gate(A));
  Transistor transistor_2 (.in(transistor_1_out), .out(R), .gate(A_NOT));
  Transistor #(.\type ("n")) transistor_3 (.in(transistor_4_out), .out(R), .gate(A));
  Transistor #(.\type ("n")) transistor_4 (.in(1'b0), .out(transistor_4_out), .gate(B));
  Transistor transistor_5 (.in(1'b1), .out(transistor_1_out), .gate(B));
  Transistor transistor_6 (.in(transistor_1_out), .out(R), .gate(B_NOT));
  Transistor #(.\type ("n")) transistor_7 (.in(transistor_8_out), .out(R), .gate(A_NOT));
  Transistor #(.\type ("n")) transistor_8 (.in(1'b0), .out(transistor_8_out), .gate(B_NOT));
  not not_1 (A_NOT, A);
  not not_2 (B_NOT, B);
endmodule

module xnor_gate (
  input  X,
  input  Y,
  output R
);

  wire NX, NY, transistor_1_out, transistor_4_out, transistor_8_out;

  Transistor transistor_1 (.in(1'b1), .out(transistor_1_out), .gate(Y));
  Transistor transistor_2 (.in(transistor_1_out), .out(R), .gate(NY));
  Transistor #(.\type ("n")) transistor_3 (.in(transistor_4_out), .out(R), .gate(X));
  Transistor #(.\type ("n")) transistor_4 (.in(1'b0), .out(transistor_4_out), .gate(NY));
  not not_1 (NX, X);
  not not_2 (NY, Y);
  Transistor transistor_5 (.in(1'b1), .out(transistor_1_out), .gate(NX));
  Transistor transistor_6 (.in(transistor_1_out), .out(R), .gate(X));
  Transistor #(.\type ("n")) transistor_7 (.in(transistor_8_out), .out(R), .gate(NX));
  Transistor #(.\type ("n")) transistor_8 (.in(1'b0), .out(transistor_8_out), .gate(Y));
endmodule

module full_adder (
  input  X,
  input  Y,
  input  CIn,
  output NSum,
  output Carry
);

  wire transistor_1_out, transistor_2_out, transistor_4_out, transistor_5_out, transistor_6_out,
       transistor_11_out, transistor_12_out, transistor_19_out, transistor_20_out, transistor_23_out,
       transistor_24_out;

  Transistor transistor_1 (.in(1'b1), .out(transistor_1_out), .gate(X));
  Transistor transistor_2 (.in(transistor_1_out), .out(transistor_2_out), .gate(Y));
  Transistor #(.\type ("n")) transistor_3 (.in(transistor_4_out), .out(transistor_2_out), .gate(X));
  Transistor #(.\type ("n")) transistor_4 (.in(1'b0), .out(transistor_4_out), .gate(Y));
  Transistor transistor_5 (.in(1'b1), .out(transistor_5_out), .gate(X));
  Transistor #(.\type ("n")) transistor_6 (.in(1'b0), .out(transistor_6_out), .gate(X));
  Transistor transistor_7 (.in(1'b1), .out(transistor_5_out), .gate(Y));
  Transistor transistor_8 (.in(transistor_5_out), .out(transistor_2_out), .gate(CIn));
  Transistor #(.\type ("n")) transistor_9 (.in(transistor_6_out), .out(transistor_2_out), .gate(CIn));
  Transistor #(.\type ("n")) transistor_10 (.in(1'b0), .out(transistor_6_out), .gate(Y));
  Transistor transistor_11 (.in(1'b1), .out(transistor_11_out), .gate(X));
  Transistor #(.\type ("n")) transistor_12 (.in(1'b0), .out(transistor_12_out), .gate(X));
  Transistor transistor_13 (.in(1'b1), .out(transistor_11_out), .gate(Y));
  Transistor #(.\type ("n")) transistor_14 (.in(1'b0), .out(transistor_12_out), .gate(Y));
  Transistor transistor_15 (.in(1'b1), .out(transistor_11_out), .gate(CIn));
  Transistor #(.\type ("n")) transistor_16 (.in(1'b0), .out(transistor_12_out), .gate(CIn));
  Transistor transistor_17 (.in(transistor_11_out), .out(NSum), .gate(transistor_2_out));
  Transistor #(.\type ("n")) transistor_18 (.in(transistor_12_out), .out(NSum), .gate(transistor_2_out));
  Transistor transistor_19 (.in(1'b1), .out(transistor_19_out), .gate(X));
  Transistor transistor_20 (.in(transistor_19_out), .out(transistor_20_out), .gate(Y));
  Transistor transistor_21 (.in(transistor_20_out), .out(NSum), .gate(CIn));
  Transistor #(.\type ("n")) transistor_22 (.in(transistor_23_out), .out(NSum), .gate(CIn));
  Transistor #(.\type ("n")) transistor_23 (.in(transistor_24_out), .out(transistor_23_out), .gate(Y));
  Transistor #(.\type ("n")) transistor_24 (.in(1'b0), .out(transistor_24_out), .gate(X));
  Transistor transistor_25 (.in(1'b1), .out(Carry), .gate(transistor_2_out));
  Transistor #(.\type ("n")) transistor_26 (.in(1'b0), .out(Carry), .gate(transistor_2_out));
endmodule

module mux_2_1 (
  input  X0,
  input  X1,
  input  S0,
  output R
);

  wire NS;

  not not_1 (NS, S0);
  // Transmission_Gate transmission_1: pin names not known; wires that end beside it: X0, S0, NS, R
  // Transmission_Gate transmission_2: pin names not known; wires that end beside it: X1, NS, S0, R

  // Other names for the same wires on the sheet: S = S0
endmodule

module mux_4_1 (
  input  X0,
  input  X1,
  input  X2,
  input  X3,
  input  S0,
  input  S1,
  output R
);

  wire NS0, NS1, transmission_1_p4, transmission_3_p4;

  not not_1 (NS0, S0);
  not not_2 (NS1, S1);
  // Transmission_Gate transmission_1: pin names not known; wires that end beside it: X0, S0, NS0, transmission_1_p4
  // Transmission_Gate transmission_2: pin names not known; wires that end beside it: X1, NS0, S0, transmission_1_p4
  // Transmission_Gate transmission_3: pin names not known; wires that end beside it: X2, S0, NS0, transmission_3_p4
  // Transmission_Gate transmission_4: pin names not known; wires that end beside it: X3, NS0, S0, transmission_3_p4
  // Transmission_Gate transmission_5: pin names not known; wires that end beside it: transmission_1_p4, S1, NS1, R
  // Transmission_Gate transmission_6: pin names not known; wires that end beside it: transmission_3_p4, NS1, S1, R
endmodule

module FullAdder (
  input  C_In,
  input  A,
  input  B,
  output Sum,
  output C_Out
);

  wire halfadder_1_halfcarry, halfadder_1_halfsum, halfadder_2_halfcarry;

  HalfAdder halfadder_1 (.A(A), .B(B), .HalfSum(halfadder_1_halfsum), .HalfCarry(halfadder_1_halfcarry));
  HalfAdder halfadder_2 (.A(C_In), .B(halfadder_1_halfsum), .HalfSum(Sum), .HalfCarry(halfadder_2_halfcarry));
  or or_1 (C_Out, halfadder_2_halfcarry, halfadder_1_halfcarry);
endmodule

module HalfAdder (
  input  A,
  input  B,
  output HalfSum,
  output HalfCarry
);

  and and_1 (HalfCarry, A, B);
  xor xor_1 (HalfSum, A, B);
endmodule
